# Fritzing sketch light-2switch_rising_edge (saved by Fritzing 0.9.3b)
breadboards: 1

parts:
  S1 = Pushbutton [package="[THT]"]
  S2 = Pushbutton [package="[THT]"]
  5V = Power plug
  REG1 = LD33 Low-Dropout Voltage Regulator
  U1 = Dual D Flip Flop, single part [part_number=4013 package="DIP (Dual Inline) [THT]"]
  1K = Resistor [tolerance=±5% resistance=1k package=THT]
  1K1 = Resistor [tolerance=±5% resistance=1k package=THT]
  1K2 = Resistor [tolerance=±5% resistance=1k package=THT]
  1K3 = Resistor [tolerance=±5% resistance=1k package=THT]
  U2 = 4011 4 x 2 Input NAND Gate, single part [part_number=CD4011BE package="DIP (Dual Inline) [THT]"]
  R1 = Resistor [tolerance=±5% resistance=1k package=THT]
  R2 = Resistor [tolerance=±5% resistance=1k package=THT]
  C1 = Electrolytic Capacitor [capacitance=10μF voltage=16V package="0605 [SMD, electrolytic]"]
  C2 = Electrolytic Capacitor [capacitance=10μF voltage=16V package="0605 [SMD, electrolytic]"]
  U3 = 4081 4 x 2 Input AND Gate, multi-part [part_number=4081 package="DIP (Dual Inline) [THT]"]
  Part1 = 4081_4_x_2_input_AND_gate_multipart_subpart1 [part_number=4081]
  U3_2 = 4081_4_x_2_input_AND_gate_multipart_subpart3 [part_number=4081]
  R3 = Resistor [tolerance=±5% resistance=1k package=THT]
  LED1 = LED - 3mm [color="White (6500K)" package="3 mm [THT]"]
  NodeMCU_v1 = NodeMCU v3 LoLin [part_number=ESP8266]

nets:
  N1: S1.Pin_1, S1.Pin_2, U1.SET2, 1K.Pin_0
  VDD: S1.Pin_3, S1.Pin_4, S2.Pin_3, S2.Pin_4, REG1.Vout, U1.VDD, U2.VDD, C2.-, U3.connector13, NodeMCU_v1.VIN
  N2: S2.Pin_1, S2.Pin_2, U1.SET1, 1K2.Pin_1
  GND: 5V.GND, REG1.GND, U1.VSS, 1K.Pin_1, 1K1.Pin_1, 1K2.Pin_0, 1K3.Pin_0, U2.GND, C1.-, U3.connector6, Part1.connector6, LED1.cathode, NodeMCU_v1.GND
  VCC: 5V.VCC, REG1.Vin
  N3: U1.Q1, U2.A1, R1.Pin_0, NodeMCU_v1.D1
  N4: U1.RESET1, U1.RESET2, 1K1.Pin_0, 1K3.Pin_1, NodeMCU_v1.D3
  N5: U1.Q2, U2.B4, R2.Pin_0, NodeMCU_v1.D2
  N6: U2.B1, U2.Q2
  N7: U2.Q1, U3.connector5
  N8: U2.A2, U2.B2, R1.Pin_1, C1.+
  N9: U2.A3, U2.B3, R2.Pin_1, C2.+
  N10: U2.Q3, U2.A4
  N11: U2.Q4, U3.connector4
  N12: U3.connector3, U3_2.connector3, R3.Pin_0, NodeMCU_v1.EN
  N13: R3.Pin_1, LED1.anode
  N14: NodeMCU_v1.D0, NodeMCU_v1.RST

notes:
  RST and DO pins of NodeMCU need to be connected in order to wake up via RTC timer after deep-sleep.
  Disconnect RST and D0 to be able to upload program from Platformio to NodeMCU
  This circuit simulates a wall light switch with two gangs. Each gang has a similar circuit. Input from the switch sets a 4013 D Flip Flop whose output feeds a 4011 NAND gate. It feeds directly the A input, and it is inversed for the B input. Also the B input is fed via a R-C circuit that creates a 10msec delay. The truth table of such a logical gate will give an output of 0 for A=1,B=0, and 1 in all other cases. The delay of the R-C circuit at input B will have as a result the creation of a 10msec low pulse when the button is pressed.
  The final outputs of the two -switches / Flip Flop / NAND gates- are combined in a 4081 AND gate. So if either switch generates a low pulse a low pulse is generated at the output of the AND gate. This low pulse is fed to the EN pin of ESP2866 thus reseting the device. As soon as ESP8266 restarts it will read the output of the Flip Flops to record if the buttons are pressed, and then immediately reset the Flip Flops so that if a button is pressed again a new restart will be generated.
  ESP8266's RST and D0 pins are connected to allow WAKE-UP after deep sleep

custom parts:
  Dual D Flip Flop, single part: CD4013BE CMOS Dual D-Type Flip-Flop
  NodeMCU v3 LoLin: NodeMCU v3 LoLin NodeMCU (http://www.nodemcu.com/) is an open source IoT platform. It includes firmware (https://nodemcu-build.com/) which runs on the ESP8266 Wi-Fi SoC from Espressif Systems, and hardware which is based on the ESP-12E module. The term "NodeMCU" by default refers to the firmware rather than the dev kits. The firmware uses the Lua scripting language. It is based on the eLua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
