# Fritzing sketch light-switch (saved by Fritzing 0.9.3b)
breadboards: 1

parts:
  Part1 = KY-019 5V Relay Module [package="Breakout board"]
  HLK-PM1 = HLK-PM01
  ACS712_Current_Sensor1 = ACS712 Current Sensor
  LED1 = LEDs [package=led10mm]
  NodeMCU_v2 = NodeMCU v3 LoLin [part_number=ESP8266]
  S2 = Round Pushbutton
  J5 = female pin header, 15 pins [form="♀ (female)"]
  J6 = female pin header, 15 pins [form="♀ (female)"]
  Part3 = Lilypad Battery Connect
  LED2 = LED - 5mm [color="Red (633nm)" package="5 mm [THT]"]
  LED3 = LED - 5mm [color="Green (555nm)" package="5 mm [THT]"]
  LED4 = LED - 5mm [color="Yellow (592nm)" package="5 mm [THT]"]
  R1 = Resistor [tolerance=±5% resistance=100 package=THT]
  R2 = Resistor [tolerance=±5% resistance=100 package=THT]
  R3 = Resistor [tolerance=±5% resistance=100 package=THT]
  R4_3_1K = Resistor [tolerance=±5% resistance=3.3k package=THT]
  R5_1_7k = Resistor [tolerance=±5% resistance=1.5k package=THT]

nets:
  N1: Part1.S, NodeMCU_v2.D0, J5.pin1
  N2: Part1.+, NodeMCU_v2.3V3, J5.pin6, J5.pin15, J6.pin11
  N3: Part1.-, HLK-PM1.-Vo, ACS712_Current_Sensor1.GND, NodeMCU_v2.GND#6, NodeMCU_v2.GND#13, NodeMCU_v2.GND#16, NodeMCU_v2.GND#33, J5.pin7, J5.pin14, J6.pin10, J6.pin14, R2.Pin_1, R3.Pin_1
  N4: Part1.Common, HLK-PM1.AC#1, Part3.-
  N5: Part1.NO, LED1.A
  N6: HLK-PM1.AC#0, LED1.C, S2.leg1
  VCC: HLK-PM1.+Vo, ACS712_Current_Sensor1.VCC, NodeMCU_v2.VIN, J6.pin15
  N7: ACS712_Current_Sensor1.OUT, R5_1_7k.Pin_1
  N8: NodeMCU_v2.D1, J5.pin2
  N9: NodeMCU_v2.D2, J5.pin3
  N10: NodeMCU_v2.D3, J5.pin4
  N11: NodeMCU_v2.D4, J5.pin5, LED2.anode
  N12: NodeMCU_v2.D5, J5.pin8, LED3.anode
  N13: NodeMCU_v2.D6, J5.pin9
  N14: NodeMCU_v2.D7, J5.pin10, LED4.anode
  N15: NodeMCU_v2.D8, J5.pin11
  N16: NodeMCU_v2.RX, J5.pin12
  N17: NodeMCU_v2.TX, J5.pin13
  N18: NodeMCU_v2.RST, J6.pin13
  N19: NodeMCU_v2.EN, J6.pin12
  N20: NodeMCU_v2.SK, J6.pin9
  N21: NodeMCU_v2.S0, J6.pin8
  N22: NodeMCU_v2.SC, J6.pin7
  N23: NodeMCU_v2.S1, J6.pin6
  N24: NodeMCU_v2.S2, J6.pin5
  N25: NodeMCU_v2.S3, J6.pin4
  N26: NodeMCU_v2.VU, J6.pin3
  N27: NodeMCU_v2.GND#41, J6.pin2
  N28: NodeMCU_v2.A0, J6.pin1, R4_3_1K.Pin_0, R5_1_7k.Pin_0
  N29: S2.leg0, Part3.+
  N30: LED2.cathode, R1.Pin_0
  N31: LED3.cathode, R3.Pin_0
  N32: LED4.cathode, R2.Pin_0

notes:
  240V AC power supply
  240V AC wall push-switch

custom parts:
  KY-019 5V Relay Module: KY-019 5V Relay module, used to control AC circuits.
  ACS712 Current Sensor: A breakout board for the Allegro ACS712 is a Hall Effect-based linear current sensor. The module operates at 5V.
  LEDs: LEDs Standard schematic elements and footprints for 5mm, 3mm, 1206, and 0603 sized LEDs. 5mm - Spark Fun Electronics SKU : COM-00529 (and others)
  NodeMCU v3 LoLin: NodeMCU v3 LoLin NodeMCU (http://www.nodemcu.com/) is an open source IoT platform. It includes firmware (https://nodemcu-build.com/) which runs on the ESP8266 Wi-Fi SoC from Espressif Systems, and hardware which is based on the ESP-12E module. The term "NodeMCU" by default refers to the firmware rather than the dev kits. The firmware uses the Lua scripting language. It is based on the eLua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
